# Fritzing sketch basementLaundryCrawlFan-ESP32 (saved by Fritzing 0.9.10b)

parts:
  ESP32_-_Back1 = ESP32 - CAM
  HLK-PM2 = HLK-PM01
  Part1 = Jtron 1 Channel Optoisolated Relay Module [package=relay]

nets:
  N1: ESP32_-_Back1.GND#7, Part1.GND
  5V: ESP32_-_Back1.5V, HLK-PM2.+Vo, Part1.VCC
  N2: ESP32_-_Back1.GPIO16, Part1.IN1
  N3: ESP32_-_Back1.GND#16, HLK-PM2.-Vo

custom parts:
  ESP32 - CAM: The ESP32-CAM has a very competitive small-size camera module that can operate independently as a minimum system with a footprint of only 27*40.5*4.5mm and a deep sleep current of up to 6mA.
